// Logisim project CA2 CIRCUIT.circ as structural Verilog: 1 circuit, main circuit main
module main (
  input  N1,
  input  N3,
  input  N2,
  input  N7,
  input  N6,
  output N22,
  output N23
);

  wire _2_1__5_out, _2_2__1_out, _2_3__4_out, _2_6__4_out;

  nand _2_2__1 (_2_2__1_out, N1, N3);
  nand _2_6__4 (_2_6__4_out, N3, N6);
  nand _2_1__5 (_2_1__5_out, N2, _2_6__4_out);
  nand _2_3__4 (_2_3__4_out, N7, _2_6__4_out);
  nand _2_5__2 (N22, _2_2__1_out, _2_1__5_out);
  nand _2_4__2 (N23, _2_1__5_out, _2_3__4_out);
endmodule
