// Logisim project CA1 CIRCUIT.circ as structural Verilog: 1 circuit, main circuit main
module main (
  input  N1,
  input  N3,
  input  N2,
  input  N7,
  input  N6,
  output N22,
  output N23
);

  wire _2_1_out, _2_2_out, _2_3_out, _2_6_out;

  nand _2_2 (_2_2_out, N1, N3);
  nand _2_6 (_2_6_out, N3, N6);
  nand _2_1 (_2_1_out, N2, _2_6_out);
  nand _2_3 (_2_3_out, N7, _2_6_out);
  nand _2_5 (N22, _2_2_out, _2_1_out);
  nand _2_4 (N23, _2_1_out, _2_3_out);
endmodule
